# Fritzing sketch Q1077-Esquema (saved by Fritzing 0.9.10b)
breadboards: 1

parts:
  S1 = Toggle Switch [package=THT]
  S2 = Pushbutton [package="[THT]"]
  Componente1 = Arduino Uno (Rev3)
  S3 = Pushbutton [package="[THT]"]
  J1 = female pin header, 5 pins [form="♀ (female)"]

nets:
  N1: S1.L1, Componente1.D4
  N2: S1.COM, S2.Pin_3, Componente1.GND, S3.Pin_3, S3.Pin_4, J1.pin4
  N3: S2.Pin_1, S2.Pin_2, Componente1.D2
  N4: Componente1.D3_PWM, S3.Pin_1, S3.Pin_2
  N5: Componente1.D5_PWM, J1.pin1
  N6: Componente1.D6_PWM, J1.pin2
  N7: Componente1.D7, J1.pin3
  N8: Componente1.5V, J1.pin5
