# Fritzing sketch Q1078-PCB (saved by Fritzing 0.9.10b)
circuit board: 9.2cm x 8.5cm
breadboards: 2

parts:
  Componente1 = Arduino Uno (Rev3)  # not connected
  S1 = Pushbutton [package="[THT]"]
  S2 = Pushbutton [package="[THT]"]
  S3 = Pushbutton [package="[THT]"]
  LED1 = LED - 5mm [color="Red (633nm)" current=0.030 package="5 mm [THT]"]
  LED2 = LED - 5mm [color="Yellow (595nm)" current=0.030 package="5 mm [THT]"]
  LED3 = LED - 5mm [color="Yellow (595nm)" current=0.030 package="5 mm [THT]"]
  LED4 = LED - 5mm [color="Yellow (595nm)" current=0.030 package="5 mm [THT]"]
  R1 = Resistor [tolerance=±5% power=0.25 resistance=180 package=THT]
  R2 = Resistor [tolerance=±5% power=0.25 resistance=180 package=THT]
  R3 = Resistor [tolerance=±5% power=0.25 resistance=180 package=THT]
  R4 = Resistor [tolerance=±5% power=0.25 resistance=180 package=THT]
  D1 = Rectifier Diode [part_number=1N4001 package="300 mil [THT]"]
  D2 = Rectifier Diode [part_number=1N4001 package="300 mil [THT]"]
  D3 = Rectifier Diode [part_number=1N4001 package="300 mil [THT]"]
  D4 = Rectifier Diode [part_number=1N4001 package="300 mil [THT]"]
  R5 = Resistor [tolerance=±5% power=0.25 resistance=100k package=THT]
  R6 = Resistor [tolerance=±5% power=0.25 resistance=1800 package=THT]
  dc_in = female pin header, 4 pins [form="♀ (female)"]
  ac_in = female pin header, 2 pins [form="♀ (female)"]
  D5 = Rectifier Diode [part_number=1N4001 package="300 mil [THT]"]
  R7 = Resistor [tolerance=±5% power=0.25 resistance=100k package=THT]
  R8 = Resistor [tolerance=±5% power=0.25 resistance=10k package=THT]
  D6 = Rectifier Diode [part_number=1N4001 package="300 mil [THT]"]
  R9 = Resistor [tolerance=±5% power=0.25 resistance=100k package=THT]
  R10 = Resistor [tolerance=±5% power=0.25 resistance=33k package=THT]
  D7 = Rectifier Diode [part_number=1N4001 package="300 mil [THT]"]
  R11 = Resistor [tolerance=±5% power=0.25 resistance=100k package=THT]
  R12 = Resistor [tolerance=±5% power=0.25 resistance=100k package=THT]
  LCD1 = LCD screen  # not connected
  lcd = female pin header, 4 pins [form="♀ (female)"]
  digital_8_13 = female pin header, 10 pins [form="♀ (female)"]
  digital_0_7 = female pin header, 8 pins [form="♀ (female)"]
  analog_a0_a5 = female pin header, 6 pins [form="♀ (female)"]
  power = female pin header, 8 pins [form="♀ (female)"]
  S4 = Pushbutton [package="[THT]"]

nets:
  N1: S1.Pin_1, S1.Pin_2, digital_0_7.pin8
  N2: S1.Pin_3, S1.Pin_4, S2.Pin_3, S2.Pin_4, S3.Pin_3, S3.Pin_4, R1.Pin_0, R2.Pin_0, R3.Pin_0, R4.Pin_0, R6.Pin_0, dc_in.pin4, R8.Pin_0, R10.Pin_0, R12.Pin_0, lcd.pin4, digital_8_13.pin7, power.pin6, power.pin7, S4.Pin_3
  N3: S2.Pin_1, digital_0_7.pin7
  N4: S3.Pin_1, digital_0_7.pin6
  N5: LED1.cathode, R1.Pin_1
  N6: LED1.anode, digital_8_13.pin4
  N7: LED2.cathode, R2.Pin_1
  N8: LED2.anode, digital_8_13.pin3
  N9: LED3.cathode, R3.Pin_1
  N10: LED3.anode, digital_8_13.pin2
  N11: LED4.cathode, R4.Pin_1
  N12: LED4.anode, digital_8_13.pin1
  N13: D1.cathode, D2.anode, ac_in.pin2
  N14: D1.anode, D4.anode
  N15: D2.cathode, D3.cathode, R5.Pin_0
  N16: D3.anode, D4.cathode, ac_in.pin1
  N17: R5.Pin_1, R6.Pin_1, analog_a0_a5.pin1
  N18: dc_in.pin1, D7.anode
  N19: dc_in.pin2, D6.anode
  N20: dc_in.pin3, D5.anode
  N21: D5.cathode, R7.Pin_0
  N22: R7.Pin_1, R8.Pin_1, analog_a0_a5.pin2
  N23: D6.cathode, R9.Pin_0
  N24: R9.Pin_1, R10.Pin_1, analog_a0_a5.pin3
  N25: D7.cathode, R11.Pin_0
  N26: R11.Pin_1, R12.Pin_1, analog_a0_a5.pin4
  N27: lcd.pin1, analog_a0_a5.pin6
  N28: lcd.pin2, analog_a0_a5.pin5
  N29: lcd.pin3, power.pin5
  N30: digital_0_7.pin5, S4.Pin_1
